# Fritzing sketch Untitled Sketch (saved by Fritzing 0.9.2b)
breadboards: 1

parts:
  Part1 = Arduino Uno (Rev3)
  J1 = Basic Servo
  J2 = Basic Servo
  S1 = Pushbutton [package="[THT]"]
  S2 = Pushbutton [package="[THT]"]
  S3 = Pushbutton [package="[THT]"]
  S4 = Pushbutton [package="[THT]"]
  R1 = Resistor [tolerance=±5% resistance=220 package=THT]
  R2 = Resistor [tolerance=±5% resistance=220 package=THT]
  R3 = Resistor [tolerance=±5% resistance=220 package=THT]
  R4 = Resistor [tolerance=±5% resistance=220 package=THT]

nets:
  N1: Part1.D9_PWM, S1.Pin_3, S1.Pin_4, R1.Pin_1
  N2: Part1.D10_PWM/SS, S4.Pin_3, S4.Pin_4, R2.Pin_1
  N3: Part1.D11_PWM/MOSI, S3.Pin_3, S3.Pin_4, R3.Pin_1
  N4: Part1.D12/MISO, S2.Pin_3, S2.Pin_4, R4.Pin_1
  GND: Part1.GND, J1.gnd, J2.gnd, R1.Pin_0, R2.Pin_0, R3.Pin_0, R4.Pin_0
  N5: Part1.D4, J2.pulse
  N6: Part1.D5_PWM, J1.pulse
  VCC: Part1.5V, J1.vcc, J2.vcc, S1.Pin_1, S1.Pin_2, S2.Pin_1, S2.Pin_2, S3.Pin_1, S3.Pin_2, S4.Pin_1, S4.Pin_2
